// Logisim project 29-bit-ALU.circ as structural Verilog: 10 circuits, main circuit main
module main (
  input  Control_1,
  input  Control_2,
  input  [28:0] A,
  input  [28:0] B,
  output [28:0] out_5,
  output Sign,
  output Zero,
  output Overflow,
  output Carry
);

  wire [28:0] adder_circuit_1_result, multiplexer_1_out, n29_bit_and_1_result, n29_bit_or_1_result;

  _29_bit_OR u_29_bit_or_1 (.A(A), .B(B), .Result(n29_bit_or_1_result));
  _29_bit_AND u_29_bit_and_1 (.A(A), .B(B), .Result(n29_bit_and_1_result));
  Adder_Circuit adder_circuit_1 (
    .Sub(Control_1), .A(A), .B(B), .Result(adder_circuit_1_result), .Carry_Out(Carry), .Overflow(Overflow));
  Multiplexer #(.width(29), .enable("false")) multiplexer_1 (
    .in0(n29_bit_or_1_result), .in1(n29_bit_and_1_result), .out(multiplexer_1_out), .sel(Control_1));
  Multiplexer #(.width(29), .enable("false")) multiplexer_2 (
    .in0(multiplexer_1_out), .in1(adder_circuit_1_result), .out(out_5), .sel(Control_2));
  _28th_bit u_28th_bit_1 (.Input(out_5), ._28th_bit(Sign));
  zero_flag zero_flag_1 (.in_1(out_5), .out_2(Zero));

  // Notes on the sheet:
  //   2107100
endmodule

module _29_bit_OR (
  input  [28:0] A,
  input  [28:0] B,
  output [28:0] Result
);

  assign Result = A | B;  // OR_Gate or_1, 29 bits wide
endmodule

module _29_bit_AND (
  input  [28:0] A,
  input  [28:0] B,
  output [28:0] Result
);

  assign Result = A & B;  // AND_Gate and_1, 29 bits wide
endmodule

module Adder_Circuit (
  input  Sub,
  input  [28:0] A,
  input  [28:0] B,
  output [28:0] Result,
  output Carry_Out,
  output Overflow
);

  wire and_1_out, and_2_out, n28th_bit_1__28th_bit, n28th_bit_2__28th_bit, n28th_bit_3__28th_bit, not_1_out,
       not_2_out, not_3_out;
  wire [28:0] n29_bit_xor_1__1_s_complement;

  _28th_bit u_28th_bit_1 (.Input(A), ._28th_bit(n28th_bit_1__28th_bit));
  _28th_bit u_28th_bit_2 (.Input(B), ._28th_bit(n28th_bit_2__28th_bit));
  _29_bit_XOR u_29_bit_xor_1 (.Control(Sub), .B(B), ._1_s_Complement(n29_bit_xor_1__1_s_complement));
  not not_1 (not_1_out, n28th_bit_1__28th_bit);
  not not_2 (not_2_out, n28th_bit_2__28th_bit);
  and and_1 (and_1_out, n28th_bit_2__28th_bit, not_3_out, n28th_bit_1__28th_bit);
  not not_3 (not_3_out, n28th_bit_3__28th_bit);
  _29_bit_parallel_adder u_29_bit_parallel_adder_1 (
    .Carry_In(Sub), .A(A), .B(n29_bit_xor_1__1_s_complement), .Result(Result), .Carry_Out(Carry_Out));
  _28th_bit u_28th_bit_3 (.Input(Result), ._28th_bit(n28th_bit_3__28th_bit));
  and and_2 (and_2_out, not_1_out, n28th_bit_3__28th_bit, not_2_out);
  or or_1 (Overflow, and_2_out, and_1_out);
endmodule

// FA
module Full_Adder (
  input  C,
  input  A,
  input  B,
  output S,
  output Carry_Out
);

  wire and_1_out, and_2_out, xor_1_out;

  and and_1 (and_1_out, B, A);
  or or_1 (Carry_Out, and_1_out, and_2_out);
  xor xor_1 (xor_1_out, A, B);
  and and_2 (and_2_out, C, xor_1_out);
  xor xor_2 (S, C, xor_1_out);
endmodule

// Adder
module _29_bit_parallel_adder (
  input  Carry_In,
  input  [28:0] A,
  input  [28:0] B,
  output [28:0] Result,
  output Carry_Out
);

  wire full_adder_1_carry_out, full_adder_2_carry_out, full_adder_3_carry_out, full_adder_4_carry_out,
       full_adder_5_carry_out, full_adder_6_carry_out, full_adder_7_carry_out, full_adder_8_carry_out,
       full_adder_9_carry_out, full_adder_10_carry_out, full_adder_11_carry_out, full_adder_12_carry_out,
       full_adder_13_carry_out, full_adder_14_carry_out, full_adder_15_carry_out, full_adder_16_carry_out,
       full_adder_17_carry_out, full_adder_18_carry_out, full_adder_19_carry_out, full_adder_20_carry_out,
       full_adder_21_carry_out, full_adder_22_carry_out, full_adder_23_carry_out, full_adder_24_carry_out,
       full_adder_25_carry_out, full_adder_26_carry_out, full_adder_27_carry_out, full_adder_28_carry_out;

  Full_Adder full_adder_1 (.C(Carry_In), .A(A[0]), .B(B[0]), .S(Result[0]), .Carry_Out(full_adder_1_carry_out));
  Full_Adder full_adder_2 (
    .C(full_adder_1_carry_out), .A(A[1]), .B(B[1]), .S(Result[1]), .Carry_Out(full_adder_2_carry_out));
  Full_Adder full_adder_3 (
    .C(full_adder_2_carry_out), .A(A[2]), .B(B[2]), .S(Result[2]), .Carry_Out(full_adder_3_carry_out));
  Full_Adder full_adder_4 (
    .C(full_adder_3_carry_out), .A(A[3]), .B(B[3]), .S(Result[3]), .Carry_Out(full_adder_4_carry_out));
  Full_Adder full_adder_5 (
    .C(full_adder_4_carry_out), .A(A[4]), .B(B[4]), .S(Result[4]), .Carry_Out(full_adder_5_carry_out));
  Full_Adder full_adder_6 (
    .C(full_adder_5_carry_out), .A(A[5]), .B(B[5]), .S(Result[5]), .Carry_Out(full_adder_6_carry_out));
  Full_Adder full_adder_7 (
    .C(full_adder_6_carry_out), .A(A[6]), .B(B[6]), .S(Result[6]), .Carry_Out(full_adder_7_carry_out));
  Full_Adder full_adder_8 (
    .C(full_adder_7_carry_out), .A(A[7]), .B(B[7]), .S(Result[7]), .Carry_Out(full_adder_8_carry_out));
  Full_Adder full_adder_9 (
    .C(full_adder_8_carry_out), .A(A[8]), .B(B[8]), .S(Result[8]), .Carry_Out(full_adder_9_carry_out));
  Full_Adder full_adder_10 (
    .C(full_adder_9_carry_out), .A(A[9]), .B(B[9]), .S(Result[9]), .Carry_Out(full_adder_10_carry_out));
  Full_Adder full_adder_11 (
    .C(full_adder_10_carry_out), .A(A[10]), .B(B[10]), .S(Result[10]), .Carry_Out(full_adder_11_carry_out));
  Full_Adder full_adder_12 (
    .C(full_adder_11_carry_out), .A(A[11]), .B(B[11]), .S(Result[11]), .Carry_Out(full_adder_12_carry_out));
  Full_Adder full_adder_13 (
    .C(full_adder_12_carry_out), .A(A[12]), .B(B[12]), .S(Result[12]), .Carry_Out(full_adder_13_carry_out));
  Full_Adder full_adder_14 (
    .C(full_adder_13_carry_out), .A(A[13]), .B(B[13]), .S(Result[13]), .Carry_Out(full_adder_14_carry_out));
  Full_Adder full_adder_15 (
    .C(full_adder_14_carry_out), .A(A[14]), .B(B[14]), .S(Result[14]), .Carry_Out(full_adder_15_carry_out));
  Full_Adder full_adder_16 (
    .C(full_adder_15_carry_out), .A(A[15]), .B(B[15]), .S(Result[15]), .Carry_Out(full_adder_16_carry_out));
  Full_Adder full_adder_17 (
    .C(full_adder_16_carry_out), .A(A[16]), .B(B[16]), .S(Result[16]), .Carry_Out(full_adder_17_carry_out));
  Full_Adder full_adder_18 (
    .C(full_adder_17_carry_out), .A(A[17]), .B(B[17]), .S(Result[17]), .Carry_Out(full_adder_18_carry_out));
  Full_Adder full_adder_19 (
    .C(full_adder_18_carry_out), .A(A[18]), .B(B[18]), .S(Result[18]), .Carry_Out(full_adder_19_carry_out));
  Full_Adder full_adder_20 (
    .C(full_adder_19_carry_out), .A(A[19]), .B(B[19]), .S(Result[19]), .Carry_Out(full_adder_20_carry_out));
  Full_Adder full_adder_21 (
    .C(full_adder_20_carry_out), .A(A[20]), .B(B[20]), .S(Result[20]), .Carry_Out(full_adder_21_carry_out));
  Full_Adder full_adder_22 (
    .C(full_adder_21_carry_out), .A(A[21]), .B(B[21]), .S(Result[21]), .Carry_Out(full_adder_22_carry_out));
  Full_Adder full_adder_23 (
    .C(full_adder_22_carry_out), .A(A[22]), .B(B[22]), .S(Result[22]), .Carry_Out(full_adder_23_carry_out));
  Full_Adder full_adder_24 (
    .C(full_adder_23_carry_out), .A(A[23]), .B(B[23]), .S(Result[23]), .Carry_Out(full_adder_24_carry_out));
  Full_Adder full_adder_25 (
    .C(full_adder_24_carry_out), .A(A[24]), .B(B[24]), .S(Result[24]), .Carry_Out(full_adder_25_carry_out));
  Full_Adder full_adder_26 (
    .C(full_adder_25_carry_out), .A(A[25]), .B(B[25]), .S(Result[25]), .Carry_Out(full_adder_26_carry_out));
  Full_Adder full_adder_27 (
    .C(full_adder_26_carry_out), .A(A[26]), .B(B[26]), .S(Result[26]), .Carry_Out(full_adder_27_carry_out));
  Full_Adder full_adder_28 (
    .C(full_adder_27_carry_out), .A(A[27]), .B(B[27]), .S(Result[27]), .Carry_Out(full_adder_28_carry_out));
  Full_Adder full_adder_29 (.C(full_adder_28_carry_out), .A(A[28]), .B(B[28]), .S(Result[28]), .Carry_Out(Carry_Out));
endmodule

module _28th_bit (
  input  [28:0] Input,
  output _28th_bit
);


  assign _28th_bit = Input[28];
endmodule

module _29_bit_XOR (
  input  Control,
  input  [28:0] B,
  output [28:0] _1_s_Complement
);

  wire [28:0] bit_extender_1_out;

  assign bit_extender_1_out = {{28{Control}}, Control};  // Bit_Extender bit_extender_1
  assign _1_s_Complement = bit_extender_1_out ^ B;  // XOR_Gate xor_1, 29 bits wide
endmodule

// zero
module zero_flag (
  input  [28:0] in_1,
  output out_2
);

  wire or_1_out;

  or or_1 (or_1_out, in_1[0], in_1[1], in_1[2], in_1[3], in_1[4], in_1[5], in_1[6], in_1[7], in_1[8], in_1[9], in_1[10], in_1[11], in_1[12], in_1[13], in_1[14], in_1[15], in_1[16], in_1[17], in_1[18], in_1[19], in_1[20], in_1[21], in_1[22], in_1[23], in_1[24], in_1[25], in_1[26], in_1[27], in_1[28]);
  not not_1 (out_2, or_1_out);
endmodule

module LAB_WORK (
  input  Add_Sub,
  input  in_2,
  input  A,
  input  in_4,
  input  B,
  input  in_6,
  input  Output,
  input  in_8,
  input  [28:0] in_9,
  input  [28:0] in_10,
  input  [28:0] in_11,
  input  [28:0] in_12,
  output Carry
);

  wire clock;
  wire [28:0] A_q, A_t, B_q, B_t, C, C_q, D, D_q, Input_A, Input_B, Input_C, Input_D, multiplexer_1_out,
       multiplexer_2_out, n29_bit_parallel_adder_1_result;

  Register #(.width(29)) u_A (.D(Input_A), .en(1'b1), .Q(A_q), .clk(clock));  // open: clr
  Register #(.width(29)) u_B (.D(Input_B), .en(1'b1), .Q(B_q), .clk(clock));  // open: clr
  Register #(.width(29)) u_C (.D(Input_C), .en(1'b1), .Q(C_q), .clk(clock));  // open: clr
  Register #(.width(29)) u_D (.D(Input_D), .en(1'b1), .Q(D_q), .clk(clock));  // open: clr
  Multiplexer #(.select(2), .width(29), .enable("false")) multiplexer_1 (
    .in0(A_q), .in1(B_q), .in2(C_q), .in3(D_q), .out(multiplexer_1_out), .sel({in_2, A}));
  Multiplexer #(.select(2), .width(29), .enable("false")) multiplexer_2 (
    .in0(A_q), .in1(B_q), .in2(C_q), .in3(D_q), .out(multiplexer_2_out), .sel({in_4, B}));
  Multiplexer #(.width(29), .enable("false")) multiplexer_3 (.in0(in_10), .in1(A_t), .out(Input_A), .sel(in_6));
  Multiplexer #(.width(29), .enable("false")) multiplexer_4 (.in0(in_12), .in1(C), .out(Input_C), .sel(in_6));
  _29_bit_parallel_adder u_29_bit_parallel_adder_1 (
    .Carry_In(Add_Sub), .A(multiplexer_1_out), .B(multiplexer_2_out),
    .Result(n29_bit_parallel_adder_1_result), .Carry_Out(Carry));
  Demultiplexer #(.select(2), .width(29), .enable("false")) demultiplexer_1 (
    .out0(A_t), .out1(B_t), .out2(C), .out3(D), .in(n29_bit_parallel_adder_1_result), .sel({Output, in_8}));
  Clock clock_1 (.out(clock));
  Multiplexer #(.width(29), .enable("false")) multiplexer_5 (.in0(in_9), .in1(B_t), .out(Input_B), .sel(in_6));
  Multiplexer #(.width(29), .enable("false")) multiplexer_6 (.in0(in_11), .in1(D), .out(Input_D), .sel(in_6));

  // Other names for the same wires on the sheet: Operate_Load = in_6

  // Notes on the sheet:
  //   21/01/2024
endmodule
